// Digital circuit cpu.dig as structural Verilog
module cpu (
  input  [31:0] IN,
  input  [3:0] REGSEL,
  input  [3:0] SEL1,
  input  [3:0] SEL2,
  input  clk,
  input  ALUEN,
  input  ALUCI,
  input  ENOUT,
  input  INMOD,
  input  LOAD,
  input  [31:0] in_14,
  input  in_15,
  input  LOAD_2,
  input  LOAD_3,
  input  ENO,
  input  LOAD_4,
  input  INVA,
  input  INVB,
  input  [31:0] INST,
  output [31:0] OUT1,
  output [31:0] OUT2,
  output [31:0] out_8,
  output [1:0] out_23,
  output [11:0] out_24,
  output [11:0] out_25,
  output [19:0] out_26,
  output [4:0] out_27,
  output [4:0] out_28,
  output [4:0] out_29,
  output [3:0] low_nibble,
  output high_bit,
  output [2:0] funct3,
  output [6:0] funct7
);

  wire comparator_1_eq, comparator_2_eq, comparator_3_eq, comparator_4_eq, comparator_5_eq, decoder_1_out_1,
       decoder_1_out_2, decoder_1_out_3, decoder_1_out_4, decoder_1_out_5, decoder_1_out_6, decoder_1_out_7,
       decoder_1_out_8, decoder_1_out_9, decoder_1_out_10, decoder_1_out_11, decoder_1_out_12,
       decoder_1_out_13, decoder_1_out_14, decoder_1_out_15, decoder_2_out_0, decoder_2_out_1,
       decoder_2_out_2, decoder_2_out_3, decoder_2_out_4, decoder_2_out_5, decoder_2_out_6, decoder_2_out_7,
       decoder_2_out_8, decoder_2_out_9, decoder_2_out_10, decoder_2_out_11, decoder_2_out_12,
       decoder_2_out_13, decoder_2_out_14, decoder_2_out_15, decoder_3_out_0, decoder_3_out_1,
       decoder_3_out_2, decoder_3_out_3, decoder_3_out_4, decoder_3_out_5, decoder_3_out_6, decoder_3_out_7,
       decoder_3_out_8, decoder_3_out_9, decoder_3_out_10, decoder_3_out_11, decoder_3_out_12,
       decoder_3_out_13, decoder_3_out_14, decoder_3_out_15, not_1_out, or_1_out, or_2_out, or_3_out,
       or_4_out, pulldown_1_out, pulldown_2_out, pullup_1_out;
  wire [4:0] demultiplexer_4_out_0;
  wire [6:0] demultiplexer_1_out_0, demultiplexer_2_out_1;
  wire [23:0] d_ff_1_q;
  wire [31:0] add_1_s, counterpreset_1_out, d_ff_2_q, d_ff_3_q, d_ff_4_q, d_ff_5_q, d_ff_6_q, d_ff_7_q,
       d_ff_8_q, d_ff_9_q, d_ff_10_q, d_ff_11_q, d_ff_12_q, d_ff_13_q, d_ff_14_q, d_ff_15_q, d_ff_16_q,
       d_ff_17_q, multiplexer_1_out, multiplexer_2_out, multiplexer_3_out, multiplexer_4_out,
       multiplexer_5_out, multiplexer_6_out, multiplexer_7_out, multiplexer_8_out, multiplexer_9_out,
       multiplexer_10_out, multiplexer_11_out, multiplexer_12_out, multiplexer_13_out, multiplexer_14_out,
       multiplexer_15_out, multiplexer_16_out, multiplexer_17_out, multiplexer_18_out, multiplexer_19_out,
       multiplexer_20_out, not_2_out, not_3_out, pulldown_3_out;
  wire [31:24] d_ff_1_q_2;

  or or_1 (or_1_out, comparator_5_eq, comparator_1_eq);
  Comparator #(.Bits(4)) comparator_1 (.a(INST[5:2]), .b(4'b1100), .eq(comparator_1_eq));  // open: gt, lt
  Demultiplexer #(.Bits(7)) demultiplexer_1 (
    .sel(or_2_out), .in(INST[31:25]), .out_0(demultiplexer_1_out_0), .out_1(out_26[19:13]));
  Demultiplexer #(.Bits(7)) demultiplexer_2 (
    .sel(or_1_out), .in(demultiplexer_1_out_0), .out_0(out_24[11:5]), .out_1(demultiplexer_2_out_1));
  Demultiplexer #(.Bits(7)) demultiplexer_3 (
    .sel(comparator_5_eq), .in(demultiplexer_2_out_1), .out_0(funct7), .out_1(out_25[11:5]));
  Demultiplexer #(.Bits(5)) demultiplexer_4 (
    .sel(or_2_out), .in(INST[24:20]), .out_0(demultiplexer_4_out_0), .out_1(out_26[12:8]));
  Demultiplexer #(.Bits(5)) demultiplexer_5 (
    .sel(or_1_out), .in(demultiplexer_4_out_0), .out_0(out_24[4:0]), .out_1(out_28));
  Demultiplexer #(.Bits(5)) demultiplexer_6 (.sel(or_2_out), .in(INST[19:15]), .out_0(out_29), .out_1(out_26[7:3]));
  Demultiplexer #(.Bits(3)) demultiplexer_7 (.sel(or_2_out), .in(INST[14:12]), .out_0(funct3), .out_1(out_26[2:0]));
  or or_2 (or_2_out, comparator_4_eq, or_3_out);
  or or_3 (or_3_out, comparator_3_eq, comparator_2_eq);
  Comparator #(.Bits(4)) comparator_2 (.a(INST[5:2]), .b(4'b1101), .eq(comparator_2_eq));  // open: gt, lt
  Comparator #(.Bits(4)) comparator_3 (.a(INST[5:2]), .b(4'b0101), .eq(comparator_3_eq));  // open: gt, lt
  Comparator #(.Bits(4)) comparator_4 (.a(INST[5:2]), .b(4'b1011), .eq(comparator_4_eq));  // open: gt, lt
  Multiplexer #(.Bits(32)) multiplexer_1 (
    .sel(LOAD_2), .in_0({d_ff_1_q_2, d_ff_1_q}), .in_1(out_8), .out(multiplexer_1_out));
  D_FF #(.Bits(32)) d_ff_1 (.D(multiplexer_1_out), .C(clk), .Q({d_ff_1_q_2, d_ff_1_q}));  // open: nQ
  Multiplexer #(.Bits(32)) multiplexer_2 (.sel(LOAD_4), .in_0(d_ff_2_q), .in_1(out_8), .out(multiplexer_2_out));
  D_FF #(.Bits(32)) d_ff_2 (.D(multiplexer_2_out), .C(clk), .Q(d_ff_2_q));  // open: nQ
  RAMSinglePort #(.AddrBits(24), .isProgramMemory("true"), .Bits(32)) ramsingleport_1 (
    .A(d_ff_1_q), .str(LOAD_3), .C(clk), .ld(ENO), .D(out_8));
  Demultiplexer #(.Bits(5)) demultiplexer_8 (
    .sel(comparator_5_eq), .in(INST[11:7]), .out_0(out_27), .out_1(out_25[4:0]));
  Comparator #(.Bits(4)) comparator_5 (.a(INST[5:2]), .b(4'b1000), .eq(comparator_5_eq));  // open: gt, lt
  assign out_8 = in_15 ? in_14 : 32'bz;  // Driver driver_1
  Decoder #(.Selector_Bits(4)) decoder_1 (
    .sel(REGSEL), .out_1(decoder_1_out_1), .out_2(decoder_1_out_2), .out_3(decoder_1_out_3),
    .out_4(decoder_1_out_4), .out_5(decoder_1_out_5), .out_6(decoder_1_out_6), .out_7(decoder_1_out_7),
    .out_8(decoder_1_out_8), .out_9(decoder_1_out_9), .out_10(decoder_1_out_10), .out_11(decoder_1_out_11),
    .out_12(decoder_1_out_12), .out_13(decoder_1_out_13), .out_14(decoder_1_out_14), .out_15(decoder_1_out_15));  // open: out_0
  Multiplexer #(.Bits(32)) multiplexer_3 (
    .sel(not_1_out), .in_0(out_8), .in_1(counterpreset_1_out), .out(multiplexer_3_out));
  not not_1 (not_1_out, INMOD);
  or or_4 (or_4_out, not_1_out, LOAD);
  CounterPreset #(.Bits(32), .isProgramCounter("true")) counterpreset_1 (
    .en(pullup_1_out), .C(clk), .dir(pulldown_1_out), .in(multiplexer_3_out), .ld(or_4_out),
    .clr(pulldown_2_out), .out(counterpreset_1_out));  // open: ovf
  PullUp pullup_1 (.out(pullup_1_out));
  PullDown pulldown_1 (.out(pulldown_1_out));
  PullDown pulldown_2 (.out(pulldown_2_out));
  assign not_2_out = ~OUT1;  // Not not_2, 32 bits wide
  assign not_3_out = ~OUT2;  // Not not_3, 32 bits wide
  assign out_8 = ENOUT ? counterpreset_1_out : 32'bz;  // Driver driver_2
  Multiplexer #(.Bits(32)) multiplexer_4 (.sel(decoder_1_out_1), .in_0(d_ff_3_q), .in_1(IN), .out(multiplexer_4_out));
  Multiplexer #(.Bits(32)) multiplexer_5 (.sel(decoder_1_out_2), .in_0(d_ff_4_q), .in_1(IN), .out(multiplexer_5_out));
  Multiplexer #(.Bits(32)) multiplexer_6 (.sel(decoder_1_out_3), .in_0(d_ff_5_q), .in_1(IN), .out(multiplexer_6_out));
  Multiplexer #(.Bits(32)) multiplexer_7 (.sel(decoder_1_out_4), .in_0(d_ff_6_q), .in_1(IN), .out(multiplexer_7_out));
  Multiplexer #(.Bits(32)) multiplexer_8 (.sel(decoder_1_out_5), .in_0(d_ff_7_q), .in_1(IN), .out(multiplexer_8_out));
  Multiplexer #(.Bits(32)) multiplexer_9 (.sel(decoder_1_out_6), .in_0(d_ff_8_q), .in_1(IN), .out(multiplexer_9_out));
  Multiplexer #(.Bits(32)) multiplexer_10 (.sel(decoder_1_out_7), .in_0(d_ff_9_q), .in_1(IN), .out(multiplexer_10_out));
  Multiplexer #(.Bits(32)) multiplexer_11 (
    .sel(decoder_1_out_8), .in_0(d_ff_10_q), .in_1(IN), .out(multiplexer_11_out));
  Multiplexer #(.Bits(32)) multiplexer_12 (
    .sel(decoder_1_out_9), .in_0(d_ff_11_q), .in_1(IN), .out(multiplexer_12_out));
  Multiplexer #(.Bits(32)) multiplexer_13 (
    .sel(decoder_1_out_10), .in_0(d_ff_12_q), .in_1(IN), .out(multiplexer_13_out));
  Multiplexer #(.Bits(32)) multiplexer_14 (
    .sel(decoder_1_out_11), .in_0(d_ff_13_q), .in_1(IN), .out(multiplexer_14_out));
  Multiplexer #(.Bits(32)) multiplexer_15 (
    .sel(decoder_1_out_12), .in_0(d_ff_14_q), .in_1(IN), .out(multiplexer_15_out));
  Multiplexer #(.Bits(32)) multiplexer_16 (
    .sel(decoder_1_out_13), .in_0(d_ff_15_q), .in_1(IN), .out(multiplexer_16_out));
  Multiplexer #(.Bits(32)) multiplexer_17 (
    .sel(decoder_1_out_14), .in_0(d_ff_16_q), .in_1(IN), .out(multiplexer_17_out));
  Multiplexer #(.Bits(32)) multiplexer_18 (
    .sel(decoder_1_out_15), .in_0(d_ff_17_q), .in_1(IN), .out(multiplexer_18_out));
  Multiplexer #(.Bits(32)) multiplexer_19 (.sel(INVA), .in_0(not_2_out), .in_1(OUT1), .out(multiplexer_19_out));
  Multiplexer #(.Bits(32)) multiplexer_20 (.sel(INVB), .in_0(not_3_out), .in_1(OUT2), .out(multiplexer_20_out));
  PullDown #(.Bits(32)) pulldown_3 (.out(pulldown_3_out));
  D_FF #(.Bits(32)) d_ff_3 (.D(multiplexer_4_out), .C(clk), .Q(d_ff_3_q));  // open: nQ
  D_FF #(.Bits(32)) d_ff_4 (.D(multiplexer_5_out), .C(clk), .Q(d_ff_4_q));  // open: nQ
  D_FF #(.Bits(32)) d_ff_5 (.D(multiplexer_6_out), .C(clk), .Q(d_ff_5_q));  // open: nQ
  D_FF #(.Bits(32)) d_ff_6 (.D(multiplexer_7_out), .C(clk), .Q(d_ff_6_q));  // open: nQ
  D_FF #(.Bits(32)) d_ff_7 (.D(multiplexer_8_out), .C(clk), .Q(d_ff_7_q));  // open: nQ
  D_FF #(.Bits(32)) d_ff_8 (.D(multiplexer_9_out), .C(clk), .Q(d_ff_8_q));  // open: nQ
  D_FF #(.Bits(32)) d_ff_9 (.D(multiplexer_10_out), .C(clk), .Q(d_ff_9_q));  // open: nQ
  D_FF #(.Bits(32)) d_ff_10 (.D(multiplexer_11_out), .C(clk), .Q(d_ff_10_q));  // open: nQ
  D_FF #(.Bits(32)) d_ff_11 (.D(multiplexer_12_out), .C(clk), .Q(d_ff_11_q));  // open: nQ
  D_FF #(.Bits(32)) d_ff_12 (.D(multiplexer_13_out), .C(clk), .Q(d_ff_12_q));  // open: nQ
  D_FF #(.Bits(32)) d_ff_13 (.D(multiplexer_14_out), .C(clk), .Q(d_ff_13_q));  // open: nQ
  D_FF #(.Bits(32)) d_ff_14 (.D(multiplexer_15_out), .C(clk), .Q(d_ff_14_q));  // open: nQ
  D_FF #(.Bits(32)) d_ff_15 (.D(multiplexer_16_out), .C(clk), .Q(d_ff_15_q));  // open: nQ
  D_FF #(.Bits(32)) d_ff_16 (.D(multiplexer_17_out), .C(clk), .Q(d_ff_16_q));  // open: nQ
  D_FF #(.Bits(32)) d_ff_17 (.D(multiplexer_18_out), .C(clk), .Q(d_ff_17_q));  // open: nQ
  Add #(.Bits(32)) add_1 (.a(multiplexer_19_out), .b(multiplexer_20_out), .c_i(ALUCI), .s(add_1_s));  // open: c_o
  assign out_8 = ALUEN ? add_1_s : 32'bz;  // Driver driver_3
  assign OUT1 = decoder_2_out_0 ? pulldown_3_out : 32'bz;  // Driver driver_4
  assign OUT2 = decoder_3_out_0 ? pulldown_3_out : 32'bz;  // Driver driver_5
  assign OUT1 = decoder_2_out_1 ? d_ff_3_q : 32'bz;  // Driver driver_6
  assign OUT2 = decoder_3_out_1 ? d_ff_3_q : 32'bz;  // Driver driver_7
  assign OUT1 = decoder_2_out_2 ? d_ff_4_q : 32'bz;  // Driver driver_8
  assign OUT2 = decoder_3_out_2 ? d_ff_4_q : 32'bz;  // Driver driver_9
  assign OUT1 = decoder_2_out_3 ? d_ff_5_q : 32'bz;  // Driver driver_10
  assign OUT2 = decoder_3_out_3 ? d_ff_5_q : 32'bz;  // Driver driver_11
  assign OUT1 = decoder_2_out_4 ? d_ff_6_q : 32'bz;  // Driver driver_12
  assign OUT2 = decoder_3_out_4 ? d_ff_6_q : 32'bz;  // Driver driver_13
  assign OUT1 = decoder_2_out_5 ? d_ff_7_q : 32'bz;  // Driver driver_14
  assign OUT2 = decoder_3_out_5 ? d_ff_7_q : 32'bz;  // Driver driver_15
  assign OUT1 = decoder_2_out_6 ? d_ff_8_q : 32'bz;  // Driver driver_16
  assign OUT2 = decoder_3_out_6 ? d_ff_8_q : 32'bz;  // Driver driver_17
  assign OUT1 = decoder_2_out_7 ? d_ff_9_q : 32'bz;  // Driver driver_18
  assign OUT2 = decoder_3_out_7 ? d_ff_9_q : 32'bz;  // Driver driver_19
  assign OUT1 = decoder_2_out_8 ? d_ff_10_q : 32'bz;  // Driver driver_20
  assign OUT2 = decoder_3_out_8 ? d_ff_10_q : 32'bz;  // Driver driver_21
  assign OUT1 = decoder_2_out_9 ? d_ff_11_q : 32'bz;  // Driver driver_22
  assign OUT2 = decoder_3_out_9 ? d_ff_11_q : 32'bz;  // Driver driver_23
  assign OUT1 = decoder_2_out_10 ? d_ff_12_q : 32'bz;  // Driver driver_24
  assign OUT2 = decoder_3_out_10 ? d_ff_12_q : 32'bz;  // Driver driver_25
  assign OUT1 = decoder_2_out_11 ? d_ff_13_q : 32'bz;  // Driver driver_26
  assign OUT2 = decoder_3_out_11 ? d_ff_13_q : 32'bz;  // Driver driver_27
  assign OUT1 = decoder_2_out_12 ? d_ff_14_q : 32'bz;  // Driver driver_28
  assign OUT2 = decoder_3_out_12 ? d_ff_14_q : 32'bz;  // Driver driver_29
  assign OUT1 = decoder_2_out_13 ? d_ff_15_q : 32'bz;  // Driver driver_30
  assign OUT2 = decoder_3_out_13 ? d_ff_15_q : 32'bz;  // Driver driver_31
  assign OUT1 = decoder_2_out_14 ? d_ff_16_q : 32'bz;  // Driver driver_32
  assign OUT2 = decoder_3_out_14 ? d_ff_16_q : 32'bz;  // Driver driver_33
  assign OUT1 = decoder_2_out_15 ? d_ff_17_q : 32'bz;  // Driver driver_34
  assign OUT2 = decoder_3_out_15 ? d_ff_17_q : 32'bz;  // Driver driver_35
  Decoder #(.Selector_Bits(4)) decoder_2 (
    .sel(SEL1), .out_0(decoder_2_out_0), .out_1(decoder_2_out_1), .out_2(decoder_2_out_2),
    .out_3(decoder_2_out_3), .out_4(decoder_2_out_4), .out_5(decoder_2_out_5), .out_6(decoder_2_out_6),
    .out_7(decoder_2_out_7), .out_8(decoder_2_out_8), .out_9(decoder_2_out_9), .out_10(decoder_2_out_10),
    .out_11(decoder_2_out_11), .out_12(decoder_2_out_12), .out_13(decoder_2_out_13),
    .out_14(decoder_2_out_14), .out_15(decoder_2_out_15));
  Decoder #(.Selector_Bits(4)) decoder_3 (
    .sel(SEL2), .out_0(decoder_3_out_0), .out_1(decoder_3_out_1), .out_2(decoder_3_out_2),
    .out_3(decoder_3_out_3), .out_4(decoder_3_out_4), .out_5(decoder_3_out_5), .out_6(decoder_3_out_6),
    .out_7(decoder_3_out_7), .out_8(decoder_3_out_8), .out_9(decoder_3_out_9), .out_10(decoder_3_out_10),
    .out_11(decoder_3_out_11), .out_12(decoder_3_out_12), .out_13(decoder_3_out_13),
    .out_14(decoder_3_out_14), .out_15(decoder_3_out_15));

  assign high_bit = INST[6];
  assign low_nibble = INST[5:2];
  assign out_23 = INST[1:0];

  // Notes on the sheet:
  //   This is here because 
  //   only the last
  //   field differs in 
  //   R/S/B types.
  //   R type
  //   ~I_type
  //   I type
  //   J type
  //   U type
  //   RD(5)
  //   RS1(5)
  //   RS2(5)
  //   IMM(20)
  //   ID
  //   S/B type
  //   Bus
endmodule
